// Logisim project 1.circ as structural Verilog: 2 circuits, main circuit main
module main (
  input  V,
  output [3:0] out_2
);

  wire and_1_out, and_2_out, and_3_out, clock_1_out, t_ff_1_qn, t_ff_2_qn, t_ff_3_qn, t_ff_4_qn;

  Clock clock_1 (.out(clock_1_out));
  and and_1 (and_1_out, t_ff_1_qn, V);
  and and_2 (and_2_out, t_ff_1_qn, t_ff_2_qn, V);
  and and_3 (and_3_out, t_ff_1_qn, t_ff_2_qn, t_ff_3_qn, V);
  T_Flip_Flop t_ff_1 (.T(V), .clk(clock_1_out), .Q(out_2[0]), .Qn(t_ff_1_qn));  // open: reset, preset
  T_Flip_Flop t_ff_2 (.T(and_1_out), .clk(clock_1_out), .Q(out_2[1]), .Qn(t_ff_2_qn));  // open: reset, preset
  T_Flip_Flop t_ff_3 (.T(and_2_out), .clk(clock_1_out), .Q(out_2[2]), .Qn(t_ff_3_qn));  // open: reset, preset
  T_Flip_Flop t_ff_4 (.T(and_3_out), .clk(clock_1_out), .Q(out_2[3]), .Qn(t_ff_4_qn));  // open: reset, preset
endmodule

module testTriggers (
  input  R,
  input  R_2,
  input  S,
  input  C,
  input  S_2,
  input  notR,
  input  notS,
  input  D,
  input  D_2,
  input  C_2,
  input  S_3,
  input  C_3,
  input  in_13,
  input  in_14,
  input  in_15,
  output Q,
  output out_17,
  output notQ,
  output out_19,
  output out_20,
  output out_21,
  output out_22,
  output out_23,
  output out_24,
  output out_25,
  output out_26,
  output out_27,
  output out_28,
  output out_29
);

  wire nand_1_out, nand_2_out, nand_3_out, nand_4_out, nand_5_out, nand_6_out, nand_15_out, nand_16_out,
       nand_17_out, nand_18_out, not_1_out;

  not not_1 (not_1_out, D);
  nand nand_1 (nand_1_out, D, C_2);
  nand nand_2 (nand_2_out, C_2, not_1_out);
  nand nand_3 (nand_3_out, out_26, C_3);
  nand nand_4 (nand_4_out, C_3, out_27);
  nand nand_5 (nand_5_out, out_29, in_13, in_14);
  nand nand_6 (nand_6_out, in_14, in_15, out_28);
  nor nor_1 (Q, R, notQ);
  nand nand_7 (out_20, notR, out_21);
  nand nand_8 (out_21, out_20, notS);
  nand nand_9 (out_26, nand_3_out, out_27);
  nor nor_2 (notQ, Q, S);
  nand nand_10 (out_22, nand_1_out, out_24);
  nand nand_11 (out_27, out_26, nand_4_out);
  nand nand_12 (out_28, nand_5_out, out_29);
  nand nand_13 (out_29, out_28, nand_6_out);
  nand nand_14 (out_24, out_22, nand_2_out);
  nand nand_15 (nand_15_out, R_2, C);
  nand nand_16 (nand_16_out, C, S_2);
  nand nand_17 (nand_17_out, D_2, S_3);
  nand nand_18 (nand_18_out, nand_17_out, S_3);
  nand nand_19 (out_17, nand_15_out, out_19);
  nand nand_20 (out_23, nand_17_out, out_25);
  nand nand_21 (out_19, out_17, nand_16_out);
  nand nand_22 (out_25, out_23, nand_18_out);

  // Notes on the sheet:
  //   R
  //   S
  //   RS trigger
  //   D trigger
  //   T trigger
  //   JK trigger
endmodule
